# Fritzing sketch js1 (saved by Fritzing 0.9.9b)
breadboards: 1

parts:
  U1 = NodeMCU V3.0
  YwRobot_Power_Supply1 = YwRobot Breadboard Power Supply [part_number=545043]
  R1 = Resistor [tolerance=±5% power=0.25 resistance=220 package=THT]
  R2 = Resistor [tolerance=±5% power=0.25 resistance=220 package=THT]
  R3 = Resistor [tolerance=±5% power=0.25 resistance=220 package=THT]
  LED1 = LED - 5mm [color="Red (633nm)" current=0.030 package="5 mm [THT]"]
  LED2 = LED - 5mm [color="Yellow (595nm)" current=0.030 package="5 mm [THT]"]
  LED3 = LED - 5mm [color="Green (565nm)" current=0.030 package="5 mm [THT]"]
  DHT1 = DHT11 Humitidy and Temperature Sensor
  Part1 = LCD1602-I2C

nets:
  N1: U1.D0, R1.Pin_1
  N2: U1.D1, Part1.SCL
  N3: U1.D2, Part1.SDA
  N4: U1.D3, R2.Pin_1
  N5: U1.D4, R3.Pin_1
  N6: U1.GND#6, U1.GND#13, U1.GND#16, U1.GND#33
  VIN: U1.Vin, YwRobot_Power_Supply1.VCC#9, YwRobot_Power_Supply1.VCC#10, DHT1.VDD, Part1.VCC
  N7: U1.S3, DHT1.DATA
  GND: U1.GND#41, YwRobot_Power_Supply1.GND#13, YwRobot_Power_Supply1.GND#14, LED1.cathode, LED2.cathode, LED3.cathode, DHT1.GND, Part1.GND
  N8: YwRobot_Power_Supply1.VCC#5, YwRobot_Power_Supply1.VCC#6
  N9: YwRobot_Power_Supply1.GND#11, YwRobot_Power_Supply1.GND#12
  N10: R1.Pin_0, LED1.anode
  N11: R2.Pin_0, LED2.anode
  N12: R3.Pin_0, LED3.anode

custom parts:
  NodeMCU V3.0: ESP8266 based NodeMCU
  YwRobot Breadboard Power Supply: The YwRobot Breadboard Power Supply (MB-V2) has two power rails; they can be 5V or 3V3. Power to the module can be provided through the female USB socket or through the A10 (female) 2.1mm power jack.
  DHT11 Humitidy and Temperature Sensor: DHT11 Humidity and Temperature Sensor
  LCD1602-I2C: A standard character display, usually with 2x16 characters. Comes in many colors with LCM1602 IIC attached.
